// Logisim project Somador carry lookahead.circ as structural Verilog: 1 circuit, main circuit main
module main (
  input  A4,
  input  B4,
  input  A3,
  input  B3,
  input  A2,
  input  B2,
  input  A1,
  input  B1,
  input  Ci1,
  output Co4,
  output S4,
  output S3,
  output S2,
  output S1
);

  wire and_1_out, and_2_out, and_3_out, and_4_out, Co1_out, Co2_out, Co3_out, G1_out, G2_out, G3_out, G4_out,
       P1_out, P2_out, P3_out, P4_out, S1_2_out, S2_2_out, S3_2_out, S4_2_out;

  xor u_S4 (S4, S4_2_out, Co3_out);
  xor u_S3 (S3, S3_2_out, Co2_out);
  xor u_S2 (S2, S2_2_out, Co1_out);
  xor u_S1 (S1, S1_2_out, Ci1);
  or u_Co4 (Co4, G4_out, and_1_out);
  and and_1 (and_1_out, P4_out, Co3_out);
  xor S4_2 (S4_2_out, A4, B4);
  xor S3_2 (S3_2_out, A3, B3);
  xor S2_2 (S2_2_out, A2, B2);
  xor S1_2 (S1_2_out, A1, B1);
  and G4 (G4_out, A4, B4);
  or P4 (P4_out, A4, B4);
  or Co3 (Co3_out, G3_out, and_2_out);
  and G3 (G3_out, A3, B3);
  or P3 (P3_out, A3, B3);
  and and_2 (and_2_out, P3_out, Co2_out);
  or Co2 (Co2_out, G2_out, and_3_out);
  and and_3 (and_3_out, P2_out, Co1_out);
  and G2 (G2_out, A2, B2);
  or P2 (P2_out, A2, B2);
  or Co1 (Co1_out, G1_out, and_4_out);
  and and_4 (and_4_out, P1_out, Ci1);
  and G1 (G1_out, A1, B1);
  or P1 (P1_out, A1, B1);
endmodule
